# Fritzing sketch arcade (saved by Fritzing 0.9.3b)
stripboards: 1

parts:
  P1-button1 = Round Pushbutton
  Composant3 = Arduino Leonardo (Rev3b)
  JOY1 = Adafruit Arcade Joystick
  P1-button2 = Round Pushbutton
  P1-button3 = Round Pushbutton
  P1-button4 = Round Pushbutton
  JOY2 = Adafruit Arcade Joystick
  P2-button4 = Round Pushbutton
  P2-button3 = Round Pushbutton
  P2-button1 = Round Pushbutton
  P2-button2 = Round Pushbutton
  1_player = Round Pushbutton
  coins = Round Pushbutton
  2_players = Round Pushbutton
  Raspberry_Pi_1 = Raspberry Pi 3 [part_number=RPI-3-V1.2]  # not connected
  R1 = Resistor [tolerance=±5% resistance=330 package=THT]
  R2 = Resistor [tolerance=±5% resistance=330 package=THT]
  R3 = Resistor [tolerance=±5% resistance=100 package=THT]
  R4 = Resistor [tolerance=±5% resistance=100 package=THT]
  R5 = Resistor [tolerance=±5% resistance=220 package=THT]
  R6 = Resistor [tolerance=±5% resistance=220 package=THT]
  R7 = Resistor [tolerance=±5% resistance=680 package=THT]
  R8 = Resistor [tolerance=±5% resistance=680 package=THT]

nets:
  N1: P1-button1.leg0, JOY1.COM, P1-button2.leg0, P1-button3.leg0, P1-button4.leg0, 1_player.leg0, coins.leg0, 2_players.leg0
  N2: P1-button1.leg1, Composant3.D4/A6
  N3: Composant3.D0/RX, JOY1.E
  N4: Composant3.D1/TX, JOY1.W
  N5: Composant3.D2/SDA, JOY1.S
  N6: Composant3.D3_PWM/SCL, JOY1.N
  N7: Composant3.D5_PWM, P1-button2.leg1
  N8: Composant3.D6_PWM/A7, JOY2.W
  N9: Composant3.D7, JOY2.S
  N10: Composant3.5V, R1.Pin_0
  N11: Composant3.GND, JOY2.E, P2-button4.leg0, R2.Pin_0
  N12: Composant3.A0, P1-button3.leg1, R1.Pin_1, R3.Pin_0
  N13: Composant3.A1, P2-button3.leg1, R2.Pin_1, R4.Pin_0
  N14: Composant3.D8/A8, JOY2.N
  N15: Composant3.D9_PWM/A9, JOY2.COM
  N16: Composant3.D10_PWM/A10, P2-button1.leg1
  N17: Composant3.D11_PWM, P2-button2.leg1
  N18: Composant3.D12/A11, coins.leg1
  N19: P1-button4.leg1, R7.Pin_0
  N20: P2-button4.leg1, R8.Pin_0
  N21: P2-button1.leg0, P2-button2.leg0
  N22: 1_player.leg1, R3.Pin_1, R5.Pin_0
  N23: 2_players.leg1, R5.Pin_1, R7.Pin_1
  N24: R4.Pin_1, R6.Pin_0
  N25: R6.Pin_1, R8.Pin_1
